// Logisim project Adder1b.circ as structural Verilog: 2 circuits, main circuit main
module main (
  input  A,
  input  B,
  input  Cin,
  output S,
  output Cout
);

  wire and_1_out, and_2_out, or_1_out, xor_1_out;

  or or_1 (or_1_out, A, B);
  and and_1 (and_1_out, or_1_out, Cin);
  and and_2 (and_2_out, A, B);
  xor xor_1 (xor_1_out, A, B);
  or or_2 (Cout, and_1_out, and_2_out);
  xor xor_2 (S, xor_1_out, Cin);
endmodule

module AddSub4b (
  input  [3:0] A,
  input  [3:0] B,
  input  Ctrl,
  output [3:0] S,
  output Cout
);

  wire main_1_cout, main_2_cout, main_3_cout, main_4_cout, xor_1_out, xor_2_out, xor_3_out, xor_4_out;

  xor xor_1 (xor_1_out, B[0], Ctrl);
  xor xor_2 (xor_2_out, B[1], Ctrl);
  xor xor_3 (xor_3_out, B[2], Ctrl);
  xor xor_4 (xor_4_out, B[3], Ctrl);
  main main_1 (.A(A[0]), .B(xor_1_out), .Cin(Ctrl), .S(S[0]), .Cout(main_1_cout));
  main main_2 (.A(A[1]), .B(xor_2_out), .Cin(main_1_cout), .S(S[1]), .Cout(main_2_cout));
  main main_3 (.A(A[2]), .B(xor_3_out), .Cin(main_2_cout), .S(S[2]), .Cout(main_3_cout));
  main main_4 (.A(A[3]), .B(xor_4_out), .Cin(main_3_cout), .S(S[3]), .Cout(main_4_cout));
  xor xor_5 (Cout, main_4_cout, Ctrl);
endmodule
